// Logisim project GreaterEqual.circ as structural Verilog: 1 circuit, main circuit main
module main (
  input  X1,
  input  X2,
  input  Y1,
  input  Y2,
  output X___Y,
  output X___Y_2
);

  wire and_1_out, and_2_out, and_3_out, and_4_out, and_5_out, and_6_out, and_7_out, not_1_out, not_2_out,
       not_3_out, not_4_out;

  not not_1 (not_1_out, X1);
  not not_2 (not_2_out, X2);
  not not_3 (not_3_out, Y1);
  not not_4 (not_4_out, Y2);
  and and_1 (and_1_out, not_1_out, Y1);
  and and_2 (and_2_out, not_1_out, not_2_out, not_3_out, Y2);
  and and_3 (and_3_out, X1, not_2_out, Y1, Y2);
  and and_4 (and_4_out, not_1_out, not_2_out, not_3_out, not_4_out);
  and and_5 (and_5_out, X1, not_2_out, Y1, not_4_out);
  and and_6 (and_6_out, not_1_out, X2, Y2, not_3_out);
  and and_7 (and_7_out, X1, X2, Y1, Y2);
  or or_1 (X___Y, and_1_out, and_2_out, and_3_out);
  or or_2 (X___Y_2, and_4_out, and_5_out, and_6_out, and_7_out);
endmodule
