// Logisim project Practica3.circ as structural Verilog: 7 circuits, main circuit ALU Completa
module ALU_1_Bit (
  input  Cin,
  input  [1:0] Op,
  input  A,
  input  B,
  output Out,
  output Cout
);

  wire adder_1_out, and_1_out, or_1_out;

  or or_1 (or_1_out, A, B);
  and and_1 (and_1_out, A, B);
  Adder adder_1 (.A(A), .B(B), .Ci(Cin), .Cout(Cout), .Out(adder_1_out));
  Multiplexer #(.select(2), .enable("false")) multiplexer_1 (
    .in0(or_1_out), .in1(and_1_out), .in2(adder_1_out), .out(Out), .sel(Op));  // open: in3
endmodule

module Adder (
  input  Ci,
  input  A,
  input  B,
  output Out,
  output Cout
);

  wire and_1_out, and_2_out, xor_1_out;

  xor xor_1 (xor_1_out, A, B);
  xor xor_2 (Out, xor_1_out, Ci);
  and and_1 (and_1_out, xor_1_out, Ci);
  and and_2 (and_2_out, B, A);
  or or_1 (Cout, and_2_out, and_1_out);
endmodule

module ALU_8_bits (
  input  in_1,
  input  [1:0] in_2,
  input  [7:0] in_3,
  input  [7:0] in_4,
  output [7:0] out_5,
  output Overflow
);

  wire alu_1_bit_1_cout, alu_1_bit_2_cout, alu_1_bit_3_cout, alu_1_bit_4_cout, alu_1_bit_5_cout,
       alu_1_bit_6_cout, alu_1_bit_7_cout;

  ALU_1_Bit alu_1_bit_1 (.A(in_3[0]), .B(in_4[0]), .Cin(in_1), .Op(in_2), .Cout(alu_1_bit_1_cout), .Out(out_5[0]));
  ALU_1_Bit alu_1_bit_2 (
    .A(in_3[1]), .B(in_4[1]), .Cin(alu_1_bit_1_cout), .Op(in_2), .Cout(alu_1_bit_2_cout), .Out(out_5[1]));
  ALU_1_Bit alu_1_bit_3 (
    .A(in_3[2]), .B(in_4[2]), .Cin(alu_1_bit_2_cout), .Op(in_2), .Cout(alu_1_bit_3_cout), .Out(out_5[2]));
  ALU_1_Bit alu_1_bit_4 (
    .A(in_3[3]), .B(in_4[3]), .Cin(alu_1_bit_3_cout), .Op(in_2), .Cout(alu_1_bit_4_cout), .Out(out_5[3]));
  ALU_1_Bit alu_1_bit_5 (
    .A(in_3[4]), .B(in_4[4]), .Cin(alu_1_bit_4_cout), .Op(in_2), .Cout(alu_1_bit_5_cout), .Out(out_5[4]));
  ALU_1_Bit alu_1_bit_6 (
    .A(in_3[5]), .B(in_4[5]), .Cin(alu_1_bit_5_cout), .Op(in_2), .Cout(alu_1_bit_6_cout), .Out(out_5[5]));
  ALU_1_Bit alu_1_bit_7 (
    .A(in_3[6]), .B(in_4[6]), .Cin(alu_1_bit_6_cout), .Op(in_2), .Cout(alu_1_bit_7_cout), .Out(out_5[6]));
  ALU_1_Bit alu_1_bit_8 (.A(in_3[7]), .B(in_4[7]), .Cin(alu_1_bit_7_cout), .Op(in_2), .Cout(Overflow), .Out(out_5[7]));
endmodule

module ALU_Sust (
  input  Cin,
  input  [1:0] Op,
  input  A,
  input  B,
  output Out,
  output Cout
);

  wire adder_1_out, adder_2_cout, adder_2_out, adder_3_cout, adder_3_out, and_1_out, not_1_out, or_1_out;

  not not_1 (not_1_out, B);
  Adder adder_1 (.A(not_1_out), .B(1'b1), .Ci(Cin), .Out(adder_1_out));  // open: Cout
  or or_1 (or_1_out, A, B);
  and and_1 (and_1_out, A, B);
  Adder adder_2 (.A(A), .B(B), .Ci(Cin), .Cout(adder_2_cout), .Out(adder_2_out));
  Adder adder_3 (.A(A), .B(adder_1_out), .Ci(Cin), .Cout(adder_3_cout), .Out(adder_3_out));
  or or_2 (Cout, adder_2_cout, adder_3_cout);
  Multiplexer #(.select(2), .enable("false")) multiplexer_1 (
    .in0(or_1_out), .in1(and_1_out), .in2(adder_2_out), .in3(adder_3_out), .out(Out), .sel(Op));
endmodule

module ALU_8_bits_Sust (
  input  Cin,
  input  [1:0] Op,
  input  [7:0] A,
  input  [7:0] B,
  output [7:0] Out,
  output Overflow
);

  wire alu_sust_1_cout, alu_sust_2_cout, alu_sust_3_cout, alu_sust_4_cout, alu_sust_5_cout, alu_sust_6_cout,
       alu_sust_7_cout;

  ALU_Sust alu_sust_1 (.A(A[0]), .B(B[0]), .Cin(Cin), .Op(Op), .Cout(alu_sust_1_cout), .Out(Out[0]));
  ALU_Sust alu_sust_2 (.A(A[1]), .B(B[1]), .Cin(alu_sust_1_cout), .Op(Op), .Cout(alu_sust_2_cout), .Out(Out[1]));
  ALU_Sust alu_sust_3 (.A(A[2]), .B(B[2]), .Cin(alu_sust_2_cout), .Op(Op), .Cout(alu_sust_3_cout), .Out(Out[2]));
  ALU_Sust alu_sust_4 (.A(A[3]), .B(B[3]), .Cin(alu_sust_3_cout), .Op(Op), .Cout(alu_sust_4_cout), .Out(Out[3]));
  ALU_Sust alu_sust_5 (.A(A[4]), .B(B[4]), .Cin(alu_sust_4_cout), .Op(Op), .Cout(alu_sust_5_cout), .Out(Out[4]));
  ALU_Sust alu_sust_6 (.A(A[5]), .B(B[5]), .Cin(alu_sust_5_cout), .Op(Op), .Cout(alu_sust_6_cout), .Out(Out[5]));
  ALU_Sust alu_sust_7 (.A(A[6]), .B(B[6]), .Cin(alu_sust_6_cout), .Op(Op), .Cout(alu_sust_7_cout), .Out(Out[6]));
  ALU_Sust alu_sust_8 (.A(A[7]), .B(B[7]), .Cin(alu_sust_7_cout), .Op(Op), .Cout(Overflow), .Out(Out[7]));
endmodule

module ALU_Completa_1_bit (
  input  Cin,
  input  [2:0] Op,
  input  A,
  input  B,
  output Out,
  output Cout
);

  wire adder_1_out, adder_2_cout, adder_2_out, adder_3_cout, adder_3_out, and_1_out, nor_1_out, not_1_out,
       not_2_out, or_1_out, xor_1_out;

  not not_1 (not_1_out, B);
  Adder adder_1 (.A(not_1_out), .B(1'b1), .Ci(Cin), .Out(adder_1_out));  // open: Cout
  nor nor_1 (nor_1_out, A, A);
  or or_1 (or_1_out, A, B);
  and and_1 (and_1_out, A, B);
  Adder adder_2 (.A(A), .B(B), .Ci(Cin), .Cout(adder_2_cout), .Out(adder_2_out));
  Adder adder_3 (.A(A), .B(adder_1_out), .Ci(Cin), .Cout(adder_3_cout), .Out(adder_3_out));
  or or_2 (Cout, adder_2_cout, adder_3_cout);
  not not_2 (not_2_out, xor_1_out);
  xor xor_1 (xor_1_out, B, A);
  Multiplexer #(.select(3), .enable("false")) multiplexer_1 (
    .in0(and_1_out), .in1(or_1_out), .in2(nor_1_out), .in3(not_2_out), .in4(adder_2_out), .in5(adder_3_out),
    .out(Out), .sel(Op));  // open: in6, in7
endmodule

module ALU_Completa (
  input  in_1,
  input  [2:0] in_2,
  input  [7:0] in_3,
  input  [7:0] in_4,
  output [7:0] out_5,
  output out_6
);

  wire alu_completa_1_bit_1_cout, alu_completa_1_bit_2_cout, alu_completa_1_bit_3_cout,
       alu_completa_1_bit_4_cout, alu_completa_1_bit_5_cout, alu_completa_1_bit_6_cout,
       alu_completa_1_bit_7_cout;

  ALU_Completa_1_bit alu_completa_1_bit_1 (
    .A(in_3[0]), .B(in_4[0]), .Cin(in_1), .Op(in_2), .Cout(alu_completa_1_bit_1_cout), .Out(out_5[0]));
  ALU_Completa_1_bit alu_completa_1_bit_2 (
    .A(in_3[1]), .B(in_4[1]), .Cin(alu_completa_1_bit_1_cout), .Op(in_2), .Cout(alu_completa_1_bit_2_cout),
    .Out(out_5[1]));
  ALU_Completa_1_bit alu_completa_1_bit_3 (
    .A(in_3[2]), .B(in_4[2]), .Cin(alu_completa_1_bit_2_cout), .Op(in_2), .Cout(alu_completa_1_bit_3_cout),
    .Out(out_5[2]));
  ALU_Completa_1_bit alu_completa_1_bit_4 (
    .A(in_3[3]), .B(in_4[3]), .Cin(alu_completa_1_bit_3_cout), .Op(in_2), .Cout(alu_completa_1_bit_4_cout),
    .Out(out_5[3]));
  ALU_Completa_1_bit alu_completa_1_bit_5 (
    .A(in_3[4]), .B(in_4[4]), .Cin(alu_completa_1_bit_4_cout), .Op(in_2), .Cout(alu_completa_1_bit_5_cout),
    .Out(out_5[4]));
  ALU_Completa_1_bit alu_completa_1_bit_6 (
    .A(in_3[5]), .B(in_4[5]), .Cin(alu_completa_1_bit_5_cout), .Op(in_2), .Cout(alu_completa_1_bit_6_cout),
    .Out(out_5[5]));
  ALU_Completa_1_bit alu_completa_1_bit_7 (
    .A(in_3[6]), .B(in_4[6]), .Cin(alu_completa_1_bit_6_cout), .Op(in_2), .Cout(alu_completa_1_bit_7_cout),
    .Out(out_5[6]));
  ALU_Completa_1_bit alu_completa_1_bit_8 (
    .A(in_3[7]), .B(in_4[7]), .Cin(alu_completa_1_bit_7_cout), .Op(in_2), .Cout(out_6), .Out(out_5[7]));
endmodule
