// Logisim project Practica04.circ as structural Verilog: 7 circuits, main circuit 9
module _9 (
  output [3:0] Salida
);

  wire and_1_out, and_2_out, and_3_out, Reloj_out;

  and and_1 (and_1_out, Salida[1], Salida[3]);
  J_K_Flip_Flop _1 (.J(1'b1), .clk(Reloj_out), .K(1'b1), .Q(Salida[0]), .reset(and_1_out));  // open: Qn, preset, en
  J_K_Flip_Flop _2 (
    .J(Salida[0]), .clk(Reloj_out), .K(Salida[0]), .Q(Salida[1]), .reset(and_1_out));  // open: Qn, preset, en
  and and_2 (and_2_out, Salida[0], Salida[1]);
  J_K_Flip_Flop _3 (
    .J(and_2_out), .clk(Reloj_out), .K(and_2_out), .Q(Salida[2]), .reset(and_1_out));  // open: Qn, preset, en
  Clock Reloj (.out(Reloj_out));
  J_K_Flip_Flop _4 (
    .J(and_3_out), .clk(Reloj_out), .K(and_3_out), .Q(Salida[3]), .reset(and_1_out));  // open: Qn, preset, en
  and and_3 (and_3_out, Salida[0], Salida[1], Salida[2]);
  Hex_Digit_Display hex_digit_display_1 (.value(Salida));  // open: dp
endmodule

module _999 (
  output [3:0] Salida,
  output [3:0] Salida_2,
  output [3:0] Salida_3
);

  wire and_1_out, and_2_out, and_3_out, and_4_out, and_5_out, and_6_out, and_7_out, and_8_out, and_9_out,
       Reloj_out;

  and and_1 (and_1_out, Salida_2[1], Salida_2[3]);
  and and_2 (and_2_out, Salida_3[1], Salida_3[3]);
  J_K_Flip_Flop _1 (.J(1'b1), .clk(Reloj_out), .K(1'b1), .Q(Salida[0]), .reset(and_3_out));  // open: Qn, preset, en
  and and_3 (and_3_out, Salida[1], Salida[3]);
  J_K_Flip_Flop _1_2 (.J(1'b1), .clk(and_3_out), .K(1'b1), .Q(Salida_2[0]), .reset(and_1_out));  // open: Qn, preset, en
  J_K_Flip_Flop _1_3 (.J(1'b1), .clk(and_1_out), .K(1'b1), .Q(Salida_3[0]), .reset(and_2_out));  // open: Qn, preset, en
  J_K_Flip_Flop _2 (
    .J(Salida_2[0]), .clk(and_3_out), .K(Salida_2[0]), .Q(Salida_2[1]), .reset(and_1_out));  // open: Qn, preset, en
  J_K_Flip_Flop _2_2 (
    .J(Salida_3[0]), .clk(and_1_out), .K(Salida_3[0]), .Q(Salida_3[1]), .reset(and_2_out));  // open: Qn, preset, en
  J_K_Flip_Flop _2_3 (
    .J(Salida[0]), .clk(Reloj_out), .K(Salida[0]), .Q(Salida[1]), .reset(and_3_out));  // open: Qn, preset, en
  and and_4 (and_4_out, Salida[0], Salida[1]);
  and and_5 (and_5_out, Salida_2[0], Salida_2[1]);
  and and_6 (and_6_out, Salida_3[0], Salida_3[1]);
  J_K_Flip_Flop _3 (
    .J(and_4_out), .clk(Reloj_out), .K(and_4_out), .Q(Salida[2]), .reset(and_3_out));  // open: Qn, preset, en
  Clock Reloj (.out(Reloj_out));
  and and_7 (and_7_out, Salida[0], Salida[1], Salida[2]);
  J_K_Flip_Flop _3_2 (
    .J(and_5_out), .clk(and_3_out), .K(and_5_out), .Q(Salida_2[2]), .reset(and_1_out));  // open: Qn, preset, en
  and and_8 (and_8_out, Salida_2[0], Salida_2[1], Salida_2[2]);
  J_K_Flip_Flop _3_3 (
    .J(and_6_out), .clk(and_1_out), .K(and_6_out), .Q(Salida_3[2]), .reset(and_2_out));  // open: Qn, preset, en
  and and_9 (and_9_out, Salida_3[0], Salida_3[1], Salida_3[2]);
  J_K_Flip_Flop _4 (
    .J(and_7_out), .clk(Reloj_out), .K(and_7_out), .Q(Salida[3]), .reset(and_3_out));  // open: Qn, preset, en
  J_K_Flip_Flop _4_2 (
    .J(and_8_out), .clk(and_3_out), .K(and_8_out), .Q(Salida_2[3]), .reset(and_1_out));  // open: Qn, preset, en
  J_K_Flip_Flop _4_3 (
    .J(and_9_out), .clk(and_1_out), .K(and_9_out), .Q(Salida_3[3]), .reset(and_2_out));  // open: Qn, preset, en
  Hex_Digit_Display hex_digit_display_1 (.value(Salida_3));  // open: dp
  Hex_Digit_Display hex_digit_display_2 (.value(Salida_2));  // open: dp
  Hex_Digit_Display hex_digit_display_3 (.value(Salida));  // open: dp
endmodule

module Registro (
  input  [7:0] in_1,
  output [7:0] out_2
);

  wire clock_1_out, not_1_out, not_2_out, not_3_out, not_4_out, not_5_out, not_6_out, not_7_out, not_8_out;

  Clock clock_1 (.out(clock_1_out));
  not not_1 (not_1_out, in_1[7]);
  S_R_Flip_Flop s_r_ff_1 (.S(in_1[7]), .clk(clock_1_out), .R(not_1_out), .Q(out_2[7]));  // open: Qn, preset, reset, en
  not not_2 (not_2_out, in_1[6]);
  S_R_Flip_Flop s_r_ff_2 (.S(in_1[6]), .clk(clock_1_out), .R(not_2_out), .Q(out_2[6]));  // open: Qn, preset, reset, en
  S_R_Flip_Flop s_r_ff_3 (.S(in_1[5]), .clk(clock_1_out), .R(not_3_out), .Q(out_2[5]));  // open: Qn, preset, reset, en
  not not_3 (not_3_out, in_1[5]);
  S_R_Flip_Flop s_r_ff_4 (.S(in_1[4]), .clk(clock_1_out), .R(not_4_out), .Q(out_2[4]));  // open: Qn, preset, reset, en
  not not_4 (not_4_out, in_1[4]);
  not not_5 (not_5_out, in_1[3]);
  S_R_Flip_Flop s_r_ff_5 (.S(in_1[3]), .clk(clock_1_out), .R(not_5_out), .Q(out_2[3]));  // open: Qn, preset, reset, en
  not not_6 (not_6_out, in_1[2]);
  S_R_Flip_Flop s_r_ff_6 (.S(in_1[2]), .clk(clock_1_out), .R(not_6_out), .Q(out_2[2]));  // open: Qn, preset, reset, en
  S_R_Flip_Flop s_r_ff_7 (.S(in_1[1]), .clk(clock_1_out), .R(not_7_out), .Q(out_2[1]));  // open: Qn, preset, reset, en
  not not_7 (not_7_out, in_1[1]);
  S_R_Flip_Flop s_r_ff_8 (.S(in_1[0]), .clk(clock_1_out), .R(not_8_out), .Q(out_2[0]));  // open: Qn, preset, reset, en
  not not_8 (not_8_out, in_1[0]);
endmodule

// R
module RegistroAND (
  input  Activar,
  input  [7:0] Entrada,
  output [7:0] Registro
);

  wire and_1_out, not_1_out, not_2_out, not_3_out, not_4_out, not_5_out, not_6_out, not_7_out, not_8_out;

  buf and_1 (and_1_out, Activar);  // AND_Gate
  not not_1 (not_1_out, Entrada[7]);
  S_R_Flip_Flop s_r_ff_1 (
    .S(Entrada[7]), .clk(and_1_out), .R(not_1_out), .Q(Registro[7]));  // open: Qn, preset, reset, en
  not not_2 (not_2_out, Entrada[6]);
  S_R_Flip_Flop s_r_ff_2 (
    .S(Entrada[6]), .clk(and_1_out), .R(not_2_out), .Q(Registro[6]));  // open: Qn, preset, reset, en
  S_R_Flip_Flop s_r_ff_3 (
    .S(Entrada[5]), .clk(and_1_out), .R(not_3_out), .Q(Registro[5]));  // open: Qn, preset, reset, en
  not not_3 (not_3_out, Entrada[5]);
  S_R_Flip_Flop s_r_ff_4 (
    .S(Entrada[4]), .clk(and_1_out), .R(not_4_out), .Q(Registro[4]));  // open: Qn, preset, reset, en
  not not_4 (not_4_out, Entrada[4]);
  not not_5 (not_5_out, Entrada[3]);
  S_R_Flip_Flop s_r_ff_5 (
    .S(Entrada[3]), .clk(and_1_out), .R(not_5_out), .Q(Registro[3]));  // open: Qn, preset, reset, en
  not not_6 (not_6_out, Entrada[2]);
  S_R_Flip_Flop s_r_ff_6 (
    .S(Entrada[2]), .clk(and_1_out), .R(not_6_out), .Q(Registro[2]));  // open: Qn, preset, reset, en
  S_R_Flip_Flop s_r_ff_7 (
    .S(Entrada[1]), .clk(and_1_out), .R(not_7_out), .Q(Registro[1]));  // open: Qn, preset, reset, en
  not not_7 (not_7_out, Entrada[1]);
  S_R_Flip_Flop s_r_ff_8 (
    .S(Entrada[0]), .clk(and_1_out), .R(not_8_out), .Q(Registro[0]));  // open: Qn, preset, reset, en
  not not_8 (not_8_out, Entrada[0]);
endmodule

module Banco_de_Registros (
  input  [1:0] Leer_1,
  input  Escribir,
  input  [7:0] DatoEscribir,
  input  [1:0] Leer_2,
  input  [1:0] Escribir_registro,
  output [7:0] Dato1,
  output [7:0] Dato2
);

  wire [7:0] demultiplexer_1_out0, demultiplexer_1_out1, demultiplexer_1_out2, demultiplexer_1_out3,
       registroand_1_registro, registroand_2_registro, registroand_3_registro, registroand_4_registro;

  Demultiplexer #(.select(2), .width(8), .disabled(0), .enable("false")) demultiplexer_1 (
    .out0(demultiplexer_1_out0), .out1(demultiplexer_1_out1), .out2(demultiplexer_1_out2),
    .out3(demultiplexer_1_out3), .in(DatoEscribir), .sel(Escribir_registro));
  RegistroAND registroand_1 (.Activar(Escribir), .Entrada(demultiplexer_1_out0), .Registro(registroand_1_registro));
  RegistroAND registroand_2 (.Activar(Escribir), .Entrada(demultiplexer_1_out1), .Registro(registroand_2_registro));
  RegistroAND registroand_3 (.Activar(Escribir), .Entrada(demultiplexer_1_out2), .Registro(registroand_3_registro));
  RegistroAND registroand_4 (.Activar(Escribir), .Entrada(demultiplexer_1_out3), .Registro(registroand_4_registro));
  Multiplexer #(.select(2), .width(8), .disabled(0)) multiplexer_1 (
    .in0(registroand_1_registro), .in1(registroand_2_registro), .in2(registroand_3_registro),
    .in3(registroand_4_registro), .out(Dato1), .sel(Leer_1));  // open: en
  Multiplexer #(.select(2), .width(8), .disabled(0)) multiplexer_2 (
    .in0(registroand_1_registro), .in1(registroand_2_registro), .in2(registroand_3_registro),
    .in3(registroand_4_registro), .out(Dato2), .sel(Leer_2));  // open: en
endmodule

module Cajita (
  input  Input,
  output TA,
  output TB
);

  wire and_1_out, and_2_out, and_3_out, and_4_out, clock_1_out, d_ff_1_qn, d_ff_2_qn, not_1_out, or_1_out;

  not not_1 (not_1_out, Input);
  and and_1 (and_1_out, d_ff_1_qn, TB, not_1_out);
  and and_2 (and_2_out, TA, d_ff_2_qn);
  and and_3 (and_3_out, TA, d_ff_2_qn, Input);
  and and_4 (and_4_out, d_ff_2_qn, not_1_out);
  or or_1 (or_1_out, and_1_out, and_2_out, and_3_out);
  Clock clock_1 (.out(clock_1_out));
  D_Flip_Flop d_ff_1 (.clk(clock_1_out), .D(or_1_out), .Q(TA), .Qn(d_ff_1_qn));  // open: preset, en, reset
  D_Flip_Flop d_ff_2 (.clk(clock_1_out), .D(and_4_out), .Q(TB), .Qn(d_ff_2_qn));  // open: preset, en, reset
endmodule

module \Autómata  (
  input  x,
  output out_2,
  output out_3
);

  Cajita cajita_1 (.Input(x), .TA(out_2), .TB(out_3));
endmodule
