// Logisim project Ejercicio.circ as structural Verilog: 2 circuits, main circuit main
module main (
  input  in_1,
  input  in_2,
  input  in_3
);

  wire clock_1_out, d_ff_1_q, d_ff_2_q, ejercicio_1_e1_2, ejercicio_1_e2_2, nand_1_out, nand_2_out;

  nand nand_1 (nand_1_out, in_1, nand_2_out);
  nand nand_2 (nand_2_out, nand_1_out, in_2);
  Ejercicio ejercicio_1 (.e1(d_ff_2_q), .e2(d_ff_1_q), .A(in_3), .E1_2(ejercicio_1_e1_2), .E2_2(ejercicio_1_e2_2));
  D_Flip_Flop d_ff_1 (.clk(clock_1_out), .D(ejercicio_1_e2_2), .Q(d_ff_1_q));  // open: Qn, preset, en, reset
  D_Flip_Flop d_ff_2 (.clk(clock_1_out), .D(ejercicio_1_e1_2), .Q(d_ff_2_q));  // open: Qn, preset, en, reset
  Clock clock_1 (.out(clock_1_out));

  // Notes on the sheet:
  //   Latch
endmodule

module Ejercicio (
  input  e1,
  input  e2,
  input  A,
  output E1_2,
  output E2_2
);

  wire and_1_out, and_2_out, not_1_out, not_2_out, not_3_out;

  not not_1 (not_1_out, e1);
  not not_2 (not_2_out, e2);
  not not_3 (not_3_out, A);
  and and_1 (and_1_out, e2, not_3_out, not_1_out);
  and and_2 (and_2_out, e1, not_2_out, A);
  and and_3 (E2_2, not_1_out, not_2_out, not_3_out);
  or or_1 (E1_2, and_1_out, and_2_out);
endmodule
